# Fritzing sketch WeatherStation (saved by Fritzing 0.9.3b)
circuit board: 5cm x 5cm
breadboards: 1

parts:
  MCU = Arduino Nano (Rev3.0)
  DHT22 = Humidity and Temperature Sensor RHT03
  UV_sensor = GUVA-S12SD UV Light Sensor
  J1 = female pin header, 2 pins [form="♀ (female)"]
  J2 = female pin header, 2 pins [form="♀ (female)"]
  Light_sensor = BH1750

nets:
  GND: MCU.GND, DHT22.GND_2, UV_sensor.GND, J2.pin1, Light_sensor.GND, Light_sensor.ADDR
  N1: MCU.D2, DHT22.Data-signal
  N2: MCU.D3, J1.pin2
  5V: MCU.5V, DHT22.Vcc, UV_sensor.5V, J2.pin2, Light_sensor.VCC
  N3: MCU.A5, Light_sensor.SCL
  N4: MCU.A4, Light_sensor.SDA
  N5: MCU.A1, UV_sensor.Out
  N6: MCU.A0, J1.pin1

notes:
  Rain sensor
  Rain Sensor

custom parts:
  GUVA-S12SD UV Light Sensor: Extend your light-sensing spectrum with this analog UV sensor module. It uses a UV photodiode, which can detect the 240-370nm range of light (which covers UVB and most of UVA spectrum). The signal level from the photodiode is very small, in the nano-ampere level, so we tossed on an opamp to amplify the signal to a more manageable volt-level.
  BH1750: Light Sensor
